// Logisim project LAB1.circ as structural Verilog
module _7404 (
  input  in_1,
  input  in_2,
  input  in_3,
  output out_4,
  output out_5,
  output out_6
);

  not not_1 (out_4, in_1);
  not not_2 (out_5, in_2);
  not not_3 (out_6, in_3);
endmodule

module main (
  input  A,
  input  B,
  input  C,
  output F_A_prime_C_AB_prime_BC
);

  wire n7404_1_out_5, n7404_1_out_6, n7408_1_out_7, n7408_1_out_8, n7408_1_out_9, n7432_1_out_9;

  _7404 u_7404_1 (.in_2(B), .in_3(A), .out_5(n7404_1_out_5), .out_6(n7404_1_out_6));  // open: in_1, out_4
  _7408 u_7408_1 (
    .in_1(B), .in_2(C), .in_3(n7404_1_out_5), .in_4(A), .in_5(C), .in_6(n7404_1_out_6),
    .out_7(n7408_1_out_7), .out_8(n7408_1_out_8), .out_9(n7408_1_out_9));
  _7432 u_7432_1 (
    .in_3(n7408_1_out_7), .in_4(n7432_1_out_9), .in_5(n7408_1_out_8), .in_6(n7408_1_out_9),
    .out_8(F_A_prime_C_AB_prime_BC), .out_9(n7432_1_out_9));  // open: in_1, in_2, out_7

  // Notes on the sheet:
  //   AB'
  //   B'
  //   A
  //   A'C
  //   C
  //   A'
  //   BC
  //   B
  //   C
  //   A'C+AB'
endmodule

module _7408 (
  input  in_1,
  input  in_2,
  input  in_3,
  input  in_4,
  input  in_5,
  input  in_6,
  output out_7,
  output out_8,
  output out_9
);

  and and_1 (out_7, in_1, in_2);
  and and_2 (out_8, in_3, in_4);
  and and_3 (out_9, in_5, in_6);
endmodule

module _7432 (
  input  in_1,
  input  in_2,
  input  in_3,
  input  in_4,
  input  in_5,
  input  in_6,
  output out_7,
  output out_8,
  output out_9
);

  or or_1 (out_7, in_1, in_2);
  or or_2 (out_8, in_3, in_4);
  or or_3 (out_9, in_5, in_6);
endmodule
