// Logisim project TABLE2 LOGISIM.circ as structural Verilog: 4 circuits, main circuit main
module main (
  input  in_1,
  input  in_2,
  input  in_3,
  output out_4
);

  wire n4075_1__9__3a, n4075_2__6__2y, n4075_2__9__3a, n7404_1__8__4y, n7404_1__10__5y, undriven, undriven_2;

  _7404 u_7404_1 (
    ._14__Vcc(in_1), ._13__6A(n4075_1__9__3a), ._11__5A(in_2), ._10__5Y(n7404_1__10__5y), ._9__4A(in_3),
    ._8__4Y(n7404_1__8__4y));  // open: _1__1A, _2__1Y, _3__2A, _4__2Y, _5__3A, _6__3Y, _7__GND, _12__6Y
  _4075 u_4075_1 (
    ._1__1A(n7404_1__10__5y), ._2__1B(n7404_1__8__4y), ._4__2B(n4075_1__9__3a), ._5__2C(in_2),
    ._6__2Y(n7404_1__8__4y), ._7__GND(undriven_2), ._11__3C(undriven), ._9__3A(n4075_1__9__3a));  // open: _3__2A, _14__Vcc, _13__1C, _12__1Y, _10__3B, _8__3Y
  _4075 u_4075_2 (
    ._1__1A(in_1), ._2__1B(in_2), ._4__2B(n7404_1__10__5y), ._5__2C(n7404_1__8__4y), ._6__2Y(n4075_2__6__2y),
    ._7__GND(in_1), ._9__3A(n4075_2__9__3a), ._8__3Y(in_3));  // open: _3__2A, _14__Vcc, _13__1C, _12__1Y, _11__3C, _10__3B
  _7411 u_7411_1 (
    ._1__1A(undriven), ._2__1B(undriven_2), ._10__3B(n4075_2__6__2y), ._9__3A(n4075_2__9__3a), ._8__3Y(out_4));  // open: _3__2A, _4__2B, _5__2C, _6__2Y, _7__GND, _14__Vcc, _13__1C, _12__1Y, _11__3C
endmodule

module _7404 (
  input  _1__1A,
  input  _14__Vcc,
  input  _13__6A,
  input  _3__2A,
  input  _11__5A,
  input  _5__3A,
  input  _9__4A,
  input  _7__GND,
  output _2__1Y,
  output _12__6Y,
  output _4__2Y,
  output _10__5Y,
  output _6__3Y,
  output _8__4Y
);

  not not_1 (_2__1Y, _1__1A);
  not not_2 (_4__2Y, _3__2A);
  not not_3 (_6__3Y, _5__3A);
  not not_4 (_12__6Y, _13__6A);
  not not_5 (_10__5Y, _11__5A);
  not not_6 (_8__4Y, _9__4A);

  // Notes on the sheet:
  //   7407: hex inverter
endmodule

module _7411 (
  input  _1__1A,
  input  _14__Vcc,
  input  _2__1B,
  input  _13__1C,
  input  _3__2A,
  input  _4__2B,
  input  _11__3C,
  input  _5__2C,
  input  _10__3B,
  input  _9__3A,
  input  _7__GND,
  output _12__1Y,
  output _6__2Y,
  output _8__3Y
);

  and and_1 (_6__2Y, _5__2C, _3__2A);
  and and_2 (_12__1Y, _2__1B, _13__1C);
  and and_3 (_8__3Y, _11__3C, _9__3A);

  // Notes on the sheet:
  //   7411: triple 3-input AND 
endmodule

module _4075 (
  input  _1__1A,
  input  _14__Vcc,
  input  _2__1B,
  input  _13__1C,
  input  _3__2A,
  input  _12__1Y,
  input  _4__2B,
  input  _11__3C,
  input  _5__2C,
  input  _7__GND,
  input  _8__3Y,
  output _10__3B,
  output _6__2Y,
  output _9__3A
);

  or or_1 (_6__2Y, _5__2C, _4__2B, _3__2A);
  or or_2 (_10__3B, _13__1C, _12__1Y, _11__3C);
  or or_3 (_9__3A, _1__1A, _2__1B, _8__3Y);
endmodule
