// Logisim project task 2 week 5.circ as structural Verilog: 1 circuit, main circuit main
module main (
  input  a1,
  input  a2,
  input  a3,
  input  a4,
  input  b1,
  input  b2,
  input  b3,
  input  b4,
  output s1,
  output c
);

  wire adder_1_cout, adder_2_cout, adder_2_out, adder_3_cout, adder_3_out, adder_4_cout, adder_4_out,
       and_1_out, and_2_out, or_1_out;

  Adder #(.width(1)) adder_1 (.a(a1), .b(b1), .out(s1), .cout(adder_1_cout));  // open: cin
  Adder #(.width(1)) adder_2 (.a(a2), .b(b2), .out(adder_2_out), .cin(adder_1_cout), .cout(adder_2_cout));
  Adder #(.width(1)) adder_3 (.a(a3), .b(b3), .out(adder_3_out), .cin(adder_2_cout), .cout(adder_3_cout));
  Adder #(.width(1)) adder_4 (.a(a4), .b(b4), .out(adder_4_out), .cin(adder_3_cout), .cout(adder_4_cout));
  and and_1 (and_1_out, adder_2_out, adder_4_out);
  and and_2 (and_2_out, adder_3_out, adder_4_out);
  or or_1 (or_1_out, and_1_out, and_2_out);
  or or_2 (c, or_1_out, adder_4_cout);

  // Notes on the sheet:
  //   s2
  //   s3
  //   s4
endmodule
