// Logisim project task 3.circ as structural Verilog: 4 circuits, main circuit 7402
module main (
  input  A,
  input  B,
  input  C,
  output out_4
);

  wire n7400_1_out_13, n7400_1_out_14;

  _7400 u_7400_1 (
    .in_5(C), .in_6(C), .in_7(n7400_1_out_13), .in_8(B), .in_9(C), .in_10(A), .out_13(n7400_1_out_13),
    .out_14(n7400_1_out_14), .out_15(n7400_1_out_14));  // open: in_1, in_2, in_3, in_4, out_11, out_12
  _7402 u_7402_1 (
    .in_5(n7400_1_out_14), .in_6(n7400_1_out_14), .out_9(out_4));  // open: in_1, in_2, in_3, in_4, out_7, out_8

  // Notes on the sheet:
  //   (ac+bc')
endmodule

module _7400 (
  input  in_1,
  input  in_2,
  input  in_3,
  input  in_4,
  input  in_5,
  input  in_6,
  input  in_7,
  input  in_8,
  input  in_9,
  input  in_10,
  output out_11,
  output out_12,
  output out_13,
  output out_14,
  output out_15
);

  nand nand_1 (out_11, in_1, in_2);
  nand nand_2 (out_12, in_3, in_4);
  nand nand_3 (out_13, in_5, in_6);
  nand nand_4 (out_14, in_7, in_8);
  nand nand_5 (out_15, in_9, in_10);
endmodule

module _7402 (
  input  in_1,
  input  in_2,
  input  in_3,
  input  in_4,
  input  in_5,
  input  in_6,
  output out_7,
  output out_8,
  output out_9
);

  nor nor_1 (out_7, in_1, in_2);
  nor nor_2 (out_8, in_3, in_4);
  nor nor_3 (out_9, in_5, in_6);
endmodule

module _7404 (
  input  in_1,
  input  in_2,
  output out_3,
  output out_4
);

  wire not_1_out, not_2_out;

  not not_1 (not_1_out, in_1);
  not not_2 (not_2_out, in_2);
endmodule
