// Logisim project task1.circ as structural Verilog: 1 circuit, main circuit main
module main (
  input  A,
  input  B,
  output out_3
);

  wire nand_1_out, nand_2_out, nand_3_out;

  nand nand_1 (nand_1_out, A, B);
  nand nand_2 (nand_2_out, A, nand_1_out);
  not nand_3 (nand_3_out, nand_1_out);  // NAND_Gate
  nand nand_4 (out_3, nand_2_out, nand_3_out);

  // Notes on the sheet:
  //   (AB)'
  //   A'+AB
  //   B'+AB
  //   (A'+AB)(B'+AB)
endmodule
