// Logisim project task4.circ as structural Verilog: 1 circuit, main circuit main
module main (
  input  A,
  input  A_2,
  input  B,
  input  A_3,
  input  B_2,
  output A_prime,
  output AB,
  output out_8
);

  wire nand_1_out, nand_2_out, nand_3_out;

  nand nand_1 (nand_1_out, A_2, B);
  nand nand_2 (nand_2_out, A_3, A_3);
  nand nand_3 (nand_3_out, B_2, B_2);
  nand nand_4 (A_prime, A, A);
  nand nand_5 (AB, nand_1_out, nand_1_out);
  nand nand_6 (out_8, nand_2_out, nand_3_out);

  // Notes on the sheet:
  //   (AB)'
  //   A+B
endmodule
