// Logisim project week 5.circ as structural Verilog: 1 circuit, main circuit main
module main (
  input  a1,
  input  a2,
  input  a3,
  input  a4,
  input  m,
  input  b1,
  input  b2,
  input  b3,
  input  b4,
  output [3:0] s
);

  wire adder_1_cout, adder_2_cout, adder_3_cout, xor_1_out, xor_2_out, xor_3_out, xor_4_out;

  xor xor_1 (xor_1_out, b1, m);
  xor xor_2 (xor_2_out, b2, m);
  xor xor_3 (xor_3_out, b4, m);
  xor xor_4 (xor_4_out, b3, m);
  Adder #(.width(1)) adder_1 (.a(a1), .b(xor_1_out), .out(s[0]), .cin(m), .cout(adder_1_cout));
  Adder #(.width(1)) adder_2 (.a(a2), .b(xor_2_out), .out(s[1]), .cin(adder_1_cout), .cout(adder_2_cout));
  Adder #(.width(1)) adder_3 (.a(a3), .b(xor_4_out), .out(s[2]), .cin(adder_2_cout), .cout(adder_3_cout));
  Adder #(.width(1)) adder_4 (.a(a4), .b(xor_3_out), .out(s[3]), .cin(adder_3_cout));  // open: cout
endmodule
