// Logisim project week 7 task 2b.circ as structural Verilog: 1 circuit, main circuit main
module main (
  input  in_1,
  input  in_2,
  input  [3:0] s,
  output out_4
);

  Multiplexer #(.select(4)) multiplexer_1 (
    .in0(in_1), .in1(in_1), .in2(in_2), .in3(in_1), .in4(in_2), .in5(in_1), .in6(in_2), .in7(in_2),
    .in8(in_1), .in9(in_1), .in10(in_2), .in11(in_2), .in12(in_2), .in13(in_2), .in14(in_1), .in15(in_1),
    .out(out_4), .sel(s));  // open: en
endmodule
