// Logisim project week7 task 2.circ as structural Verilog: 1 circuit, main circuit main
module main (
  input  _0,
  input  _1,
  input  _2,
  input  _3,
  input  _4,
  input  _5,
  input  _6,
  input  [2:0] s,
  input  _7,
  output out_10
);

  Multiplexer #(.select(3)) multiplexer_1 (
    .in0(_0), .in1(_1), .in2(_2), .in3(_3), .in4(_4), .in5(_5), .in6(_6), .in7(_7), .out(out_10), .sel(s));  // open: en

  // Notes on the sheet:
  //   L
  //   L
  //   L
  //   L
  //   L
  //   L
  //   L
  //   L
endmodule
