// Logisim project week7.circ as structural Verilog: 1 circuit, main circuit main
module main (
  input  E,
  input  _10,
  input  _11,
  input  _12,
  input  _13,
  input  _14,
  input  _15,
  output out_8
);

  wire and_1_out, and_2_out, and_3_out, and_4_out, not_1_out, not_2_out;

  not not_1 (not_1_out, _14);
  not not_2 (not_2_out, _15);
  and and_1 (and_1_out, _10, not_1_out, not_2_out, E);
  and and_2 (and_2_out, _11, not_1_out, _15, E);
  and and_3 (and_3_out, _12, _14, not_2_out, E);
  and and_4 (and_4_out, _13, _15, _14, E);
  or or_1 (out_8, and_1_out, and_2_out, and_3_out, and_4_out);
endmodule
